# Fritzing sketch Accel2CV-noLPF (saved by Fritzing 0.9.4)
breadboards: 1

parts:
  パーツ1 = Triple Axis Accelerometer Breakout - ADXL345
  パーツ3 = Arduino Uno (Rev3)
  U1 = 3.5mm Audio Jack [package=audio-jack-3.5mm-smd]

nets:
  GND: パーツ1.GND, パーツ3.GND, U1.SLEEVE
  VCC: パーツ1.VCC, パーツ3.3V3
  N1: パーツ1.SDA, パーツ3.A4/SDA
  N2: パーツ1.SCL, パーツ3.A5/SCL
  N3: パーツ3.D9_PWM, U1.RIGHT, U1.LEFT

notes:
  CVへ
